// Logisim project AdderSubCircuit.circ as structural Verilog: 1 circuit, main circuit main
module main (
  input  B4,
  input  B3,
  input  B2,
  input  in_4
);

  _74283 #(.ShowInternalStructure("true")) u_74283_1 ();  // open: pin1, pin2, pin3, pin4, pin5, pin6, pin7, pin15, pin14, pin13, pin12, pin11, pin10, pin9
endmodule
